# Fritzing sketch riego automatizado (saved by Fritzing 0.8.7b)
breadboards: 1

parts:
  Part1 = Real Time Clock Module - DS1307 RTC Breakout Board
  Arduino1 = Arduino Uno (Rev3)
  U1 = 2-Channel 5v Relay Shield [package=relay-2ch5v10a]
  V1 = DC Power [voltage=5]
  J1 = Power Jack [package=power_jack_pth]
  M1 = DC Motor

nets:
  5V: Part1.5V, Arduino1.5V, U1.VCC
  GND: Part1.GND, Arduino1.GND, U1.GND
  N1: Part1.SCL, Arduino1.A5/SCL
  N2: Part1.SDA, Arduino1.A4/SDA
  N3: Arduino1.D8, U1.IN1
  N4: U1.K1-In, J1.PWR
  N5: U1.K1-On, V1.V-, M1.pin_2
  N6: J1.GND, M1.pin_1

notes:
  Fuente 12V.
  Bomba de Agua

custom parts:
  2-Channel 5v Relay Shield: 2 Channel 5v Relay Shield w. 2x SPD-06VDC-SD-C
